// Logisim project Lab6Final.circ as structural Verilog: 20 circuits, main circuit Y86_Architecture
module Y86_Architecture (
  output [3:0] ifun,
  output [63:0] valm,
  output [63:0] valB,
  output [3:0] rB,
  output [63:0] valA,
  output [63:0] vale,
  output [3:0] rA,
  output [3:0] destE,
  output [3:0] icode,
  output [3:0] destM,
  output [3:0] sourceB,
  output [63:0] valC,
  output [3:0] sourceA,
  output [63:0] valP,
  output [11:0] out_15
);

  wire and_1_out, clock_1_out, comparator_1_eq, comparator_2_gt, comparator_3_gt, comparator_4_gt,
       controlled_buffer_1_out, demultiplexer_1_out12, demultiplexer_1_out13, execute_unit_1_of_flag,
       execute_unit_1_setcc, execute_unit_1_sf, execute_unit_1_zf, not_1_out, totalcc_1_finalcc;
  wire [3:0] clocktracker_1_cyclecount;
  wire [11:0] register_1_q;

  Clock clock_1 (.out(clock_1_out));
  Register #(.width(12)) register_1 (
    .D(out_15), .en(comparator_2_gt), .clk(controlled_buffer_1_out), .Q(register_1_q));  // open: clr
  Comparator #(.mode("unsigned"), .width(4)) comparator_1 (
    .a(icode), .b(4'b0000), .eq(comparator_1_eq));  // open: gt, lt
  Fetch_Unit fetch_unit_1 (
    .clk(controlled_buffer_1_out), .addr(register_1_q), .icode(icode), .ifun(ifun), .rA(rA), .rB(rB),
    .valC(valC), .valP(valP));
  clockTracker clocktracker_1 (.clk(controlled_buffer_1_out), .cycleCount(clocktracker_1_cyclecount));
  Demultiplexer #(.select(4)) demultiplexer_1 (
    .out12(demultiplexer_1_out12), .out13(demultiplexer_1_out13), .in(controlled_buffer_1_out),
    .sel(clocktracker_1_cyclecount));  // open: out0, out1, out2, out3, out4, out5, out6, out7, out8, out9, out10, out11, out14, out15
  Comparator #(.mode("unsigned"), .width(4)) comparator_2 (
    .a(clocktracker_1_cyclecount), .b(4'b1101), .gt(comparator_2_gt));  // open: eq, lt
  Comparator #(.width(12)) comparator_3 (.a(out_15), .b({12{1'b0}}), .gt(comparator_3_gt));  // open: eq, lt
  and and_1 (and_1_out, comparator_1_eq, comparator_3_gt);
  srcA srca_1 (.icode(icode), .rA(rA), .src_A(sourceA));
  srcB srcb_1 (.icode(icode), .rB(rB), .src_B(sourceB));
  dstM dstm_1 (.icode(icode), .rA(rA), .dst_M(destM));
  dstE dste_1 (.icode(icode), .rB(rB), .dst_E(destE));
  Comparator #(.mode("unsigned"), .width(4)) comparator_4 (
    .a(clocktracker_1_cyclecount), .b(4'b1011), .gt(comparator_4_gt));  // open: eq, lt
  assign controlled_buffer_1_out = not_1_out ? clock_1_out : 1'bz;  // Controlled_Buffer controlled_buffer_1
  not not_1 (not_1_out, and_1_out);
  Decode_Unit decode_unit_1 (
    .dstE(destE), .valE(vale), .srcA(sourceA), .srcB(sourceB), .dstM(destM), .valM(valm),
    .CLK(demultiplexer_1_out12), .WE(comparator_4_gt), .valA(valA), .valB(valB));
  Execute_unit execute_unit_1 (
    .icode(icode), .ValA(valA), .ValC(valC), .ValB(valB), .ifun(ifun), .clk(demultiplexer_1_out12),
    .setCC(execute_unit_1_setcc), .zf(execute_unit_1_zf), .valE(vale), .SF(execute_unit_1_sf),
    .OF_Flag(execute_unit_1_of_flag));  // open: cf
  totalCC totalcc_1 (
    .ZF(execute_unit_1_zf), .SF(execute_unit_1_sf), .OFflag(execute_unit_1_of_flag), .ifun(ifun),
    .icode(icode), .SetCC(execute_unit_1_setcc), .FinalCC(totalcc_1_finalcc));
  memory memory_1 (.valP(valP), .CLK(demultiplexer_1_out13), .valA(valA), .icode(icode), .valE(vale), .ValM(valm));
  PC_update pc_update_1 (.valC(valC), .Cnd(totalcc_1_finalcc), .valM(valm), .valP(valP), .icode(icode), .newPC(out_15));
endmodule

module Fetch_Unit (
  input  clk,
  input  [11:0] addr,
  output [3:0] icode,
  output [3:0] ifun,
  output [3:0] rA,
  output [3:0] rB,
  output [63:0] valC,
  output [63:0] valP
);

  wire setflags1_1_needregids, setflags1_1_needvalc;
  wire [3:0] instruction_memory_1_byte1, instruction_memory_1_byte1_2;
  wire [7:0] instruction_memory_1_byte2, instruction_memory_1_byte3, instruction_memory_1_byte4,
       instruction_memory_1_byte5, instruction_memory_1_byte6, instruction_memory_1_byte7,
       instruction_memory_1_byte8, instruction_memory_1_byte9;
  wire [63:0] next_pc_1_valp;

  Instruction_Memory instruction_memory_1 (
    .clk(clk), .address(addr), .byte0({icode, ifun}),
    .byte1({instruction_memory_1_byte1_2, instruction_memory_1_byte1}), .byte2(instruction_memory_1_byte2),
    .byte3(instruction_memory_1_byte3), .byte4(instruction_memory_1_byte4),
    .byte5(instruction_memory_1_byte5), .byte6(instruction_memory_1_byte6),
    .byte7(instruction_memory_1_byte7), .byte8(instruction_memory_1_byte8), .byte9(instruction_memory_1_byte9));
  SetFlags1 setflags1_1 (.Byte0({icode, ifun}), .NeedValC(setflags1_1_needvalc), .NeedRegIds(setflags1_1_needregids));
  Multiplexer #(.select(4), .width(4)) multiplexer_1 (
    .in0(4'b1111), .in1(4'b1111), .in2(instruction_memory_1_byte1_2), .in3(4'b1111),
    .in4(instruction_memory_1_byte1_2), .in5(instruction_memory_1_byte1_2),
    .in6(instruction_memory_1_byte1_2), .in7(4'b1111), .in8(4'b1111), .in9(4'b1111),
    .in10(instruction_memory_1_byte1_2), .in11(instruction_memory_1_byte1_2), .out(rA), .sel(icode));  // open: in12, in13, in14, in15
  Multiplexer #(.select(4), .width(4)) multiplexer_2 (
    .in0(4'b1111), .in1(4'b1111), .in2(instruction_memory_1_byte1), .in3(instruction_memory_1_byte1),
    .in4(instruction_memory_1_byte1), .in5(instruction_memory_1_byte1), .in6(instruction_memory_1_byte1),
    .in7(4'b1111), .in8(4'b1111), .in9(4'b1111), .in10(instruction_memory_1_byte1),
    .in11(instruction_memory_1_byte1), .out(rB), .sel(icode));  // open: in12, in13, in14, in15
  Multiplexer #(.select(4), .width(64)) multiplexer_3 (
    .in0({64{1'b0}}), .in1({64{1'b0}}), .in2({64{1'b0}}),
    .in3({instruction_memory_1_byte9, instruction_memory_1_byte8, instruction_memory_1_byte7, instruction_memory_1_byte6, instruction_memory_1_byte5, instruction_memory_1_byte4, instruction_memory_1_byte3, instruction_memory_1_byte2}),
    .in4({instruction_memory_1_byte9, instruction_memory_1_byte8, instruction_memory_1_byte7, instruction_memory_1_byte6, instruction_memory_1_byte5, instruction_memory_1_byte4, instruction_memory_1_byte3, instruction_memory_1_byte2}),
    .in5({instruction_memory_1_byte9, instruction_memory_1_byte8, instruction_memory_1_byte7, instruction_memory_1_byte6, instruction_memory_1_byte5, instruction_memory_1_byte4, instruction_memory_1_byte3, instruction_memory_1_byte2}),
    .in6({64{1'b0}}),
    .in7({instruction_memory_1_byte8, instruction_memory_1_byte7, instruction_memory_1_byte6, instruction_memory_1_byte5, instruction_memory_1_byte4, instruction_memory_1_byte3, instruction_memory_1_byte2, instruction_memory_1_byte1_2, instruction_memory_1_byte1}),
    .in8({instruction_memory_1_byte8, instruction_memory_1_byte7, instruction_memory_1_byte6, instruction_memory_1_byte5, instruction_memory_1_byte4, instruction_memory_1_byte3, instruction_memory_1_byte2, instruction_memory_1_byte1_2, instruction_memory_1_byte1}),
    .in9({64{1'b0}}), .in10({64{1'b0}}), .in11({64{1'b0}}), .out(valC), .sel(icode));  // open: in12, in13, in14, in15
  next_PC next_pc_1 (
    .NeedValC(setflags1_1_needvalc), .NeedRegids(setflags1_1_needregids), .PC(addr), .valP(next_pc_1_valp));
  Register #(.width(64)) register_1 (.D(next_pc_1_valp), .clk(clk), .Q(valP));  // open: en, clr

  // Notes on the sheet:
  //   r_A mux
  //   r_B mux
  //   val_C_mux
endmodule

module Instruction_Memory (
  input  clk,
  input  [11:0] address,
  output [7:0] byte0,
  output [7:0] byte1,
  output [7:0] byte2,
  output [7:0] byte3,
  output [7:0] byte4,
  output [7:0] byte5,
  output [7:0] byte6,
  output [7:0] byte7,
  output [7:0] byte8,
  output [7:0] byte9
);

  wire comparator_1_eq, comparator_1_lt, comparator_2_eq, comparator_3_eq, comparator_4_eq, comparator_5_eq,
       comparator_6_eq, comparator_7_eq, comparator_8_eq, comparator_9_eq, comparator_10_eq,
       comparator_11_eq, comparator_12_eq, controlled_buffer_1_out, or_1_out;
  wire [3:0] clocktracker_1_cyclecount, counter_2_q;
  wire [7:0] demultiplexer_1_out0, demultiplexer_1_out1, demultiplexer_1_out2, demultiplexer_1_out3,
       demultiplexer_1_out4, demultiplexer_1_out5, demultiplexer_1_out6, demultiplexer_1_out7,
       demultiplexer_1_out8, demultiplexer_1_out9, rom_1_data;
  wire [11:0] adder_1_out, counter_1_q;

  clockTracker clocktracker_1 (.clk(clk), .cycleCount(clocktracker_1_cyclecount));
  assign controlled_buffer_1_out = comparator_1_lt ? clk : 1'bz;  // Controlled_Buffer controlled_buffer_1
  Comparator #(.mode("unsigned"), .width(4)) comparator_1 (
    .a(clocktracker_1_cyclecount), .b(4'b1010), .eq(comparator_1_eq), .lt(comparator_1_lt));  // open: gt
  Counter #(.max('hfff), .width(12)) counter_1 (
    .clr(comparator_2_eq), .load(comparator_1_eq), .clk(controlled_buffer_1_out), .Q(counter_1_q));  // open: up, count, D, carry
  Counter #(.max('hf), .width(4)) counter_2 (
    .clr(or_1_out), .clk(controlled_buffer_1_out), .Q(counter_2_q));  // open: load, up, count, D, carry
  or or_1 (or_1_out, comparator_2_eq, comparator_1_eq);
  ROM #(.addrWidth(12)) rom_1 (.addr(adder_1_out), .data(rom_1_data));
  Adder #(.width(12)) adder_1 (.a(counter_1_q), .b(address), .out(adder_1_out));  // open: cin, cout
  Comparator #(.width(12)) comparator_2 (.a(12'ha), .b(counter_1_q), .eq(comparator_2_eq));  // open: gt, lt
  Demultiplexer #(.select(4), .width(8)) demultiplexer_1 (
    .out0(demultiplexer_1_out0), .out1(demultiplexer_1_out1), .out2(demultiplexer_1_out2),
    .out3(demultiplexer_1_out3), .out4(demultiplexer_1_out4), .out5(demultiplexer_1_out5),
    .out6(demultiplexer_1_out6), .out7(demultiplexer_1_out7), .out8(demultiplexer_1_out8),
    .out9(demultiplexer_1_out9), .in(rom_1_data), .sel(counter_2_q));  // open: out10, out11, out12, out13, out14, out15
  Comparator #(.width(4)) comparator_3 (.a(counter_2_q), .b(4'b0000), .eq(comparator_3_eq));  // open: gt, lt
  Register register_1 (
    .D(demultiplexer_1_out0), .en(comparator_3_eq), .clk(controlled_buffer_1_out), .Q(byte0));  // open: clr
  Comparator #(.width(4)) comparator_4 (.a(counter_2_q), .b(4'b0001), .eq(comparator_4_eq));  // open: gt, lt
  Comparator #(.width(4)) comparator_5 (.a(counter_2_q), .b(4'b0010), .eq(comparator_5_eq));  // open: gt, lt
  Comparator #(.width(4)) comparator_6 (.a(counter_2_q), .b(4'b0011), .eq(comparator_6_eq));  // open: gt, lt
  Comparator #(.width(4)) comparator_7 (.a(counter_2_q), .b(4'b0100), .eq(comparator_7_eq));  // open: gt, lt
  Comparator #(.width(4)) comparator_8 (.a(counter_2_q), .b(4'b0101), .eq(comparator_8_eq));  // open: gt, lt
  Comparator #(.width(4)) comparator_9 (.a(counter_2_q), .b(4'b0110), .eq(comparator_9_eq));  // open: gt, lt
  Comparator #(.width(4)) comparator_10 (.a(counter_2_q), .b(4'b0111), .eq(comparator_10_eq));  // open: gt, lt
  Comparator #(.width(4)) comparator_11 (.a(counter_2_q), .b(4'b1000), .eq(comparator_11_eq));  // open: gt, lt
  Comparator #(.width(4)) comparator_12 (.a(counter_2_q), .b(4'b1001), .eq(comparator_12_eq));  // open: gt, lt
  Register register_2 (
    .D(demultiplexer_1_out1), .en(comparator_4_eq), .clk(controlled_buffer_1_out), .Q(byte1));  // open: clr
  Register register_3 (
    .D(demultiplexer_1_out2), .en(comparator_5_eq), .clk(controlled_buffer_1_out), .Q(byte2));  // open: clr
  Register register_4 (
    .D(demultiplexer_1_out3), .en(comparator_6_eq), .clk(controlled_buffer_1_out), .Q(byte3));  // open: clr
  Register register_5 (
    .D(demultiplexer_1_out4), .en(comparator_7_eq), .clk(controlled_buffer_1_out), .Q(byte4));  // open: clr
  Register register_6 (
    .D(demultiplexer_1_out5), .en(comparator_8_eq), .clk(controlled_buffer_1_out), .Q(byte5));  // open: clr
  Register register_7 (
    .D(demultiplexer_1_out6), .en(comparator_9_eq), .clk(controlled_buffer_1_out), .Q(byte6));  // open: clr
  Register register_8 (
    .D(demultiplexer_1_out7), .en(comparator_10_eq), .clk(controlled_buffer_1_out), .Q(byte7));  // open: clr
  Register register_9 (
    .D(demultiplexer_1_out8), .en(comparator_11_eq), .clk(controlled_buffer_1_out), .Q(byte8));  // open: clr
  Register register_10 (
    .D(demultiplexer_1_out9), .en(comparator_12_eq), .clk(controlled_buffer_1_out), .Q(byte9));  // open: clr

  // Notes on the sheet:
  //   left operand
  //   right operand
  //   contents of rom_1 (hex, n*v repeats v):
  //   30 f4 0 1 6*0 30 f2 1 7*0 30 f3 2 7*0 20 3a 60 3a 10 a0 2f 61 32 b0 2f 71 5f 7*0 30 f5 3 7*0 40 5a
  //   8*0 61 52 30 f7 4 7*0 60 73 50 93 9*0 30 f2 7 7*0 30 f8 1 7*0 60 83
endmodule

module SetFlags (
  input  [7:0] Byte0,
  output NeedValC,
  output NeedRegIds,
  output InstrValid
);

  wire and_2_out, and_3_out, and_4_out, and_5_out, and_6_out, and_7_out, and_8_out, and_9_out, and_10_out,
       and_11_out, and_12_out, and_13_out, and_14_out, and_15_out, and_16_out, and_17_out, and_18_out,
       and_19_out, and_20_out, not_1_out, not_2_out, not_3_out, not_4_out, not_5_out, not_6_out, not_7_out,
       not_8_out;

  // AND_Gate and_1 has open pins: in0=not_4_out, in1=Byte0[2], in2=Byte0[1], out=open
  not not_1 (not_1_out, Byte0[0]);
  not not_2 (not_2_out, Byte0[1]);
  not not_3 (not_3_out, Byte0[2]);
  not not_4 (not_4_out, Byte0[3]);
  not not_5 (not_5_out, Byte0[7]);
  not not_6 (not_6_out, Byte0[6]);
  not not_7 (not_7_out, Byte0[5]);
  not not_8 (not_8_out, Byte0[4]);
  and and_2 (and_2_out, not_1_out, not_2_out, not_3_out, not_4_out, not_5_out, Byte0[5], Byte0[4]);
  and and_3 (and_3_out, not_1_out, not_2_out, not_3_out, not_4_out, not_5_out, Byte0[6], not_7_out);
  and and_4 (and_4_out, not_1_out, not_2_out, not_5_out, Byte0[6], Byte0[5], Byte0[4]);
  and and_5 (and_5_out, not_1_out, not_3_out, not_5_out, Byte0[6], Byte0[5], Byte0[4]);
  and and_6 (and_6_out, not_1_out, not_4_out, not_5_out, Byte0[6], Byte0[5], Byte0[4]);
  and and_7 (and_7_out, not_1_out, not_2_out, not_3_out, not_4_out, Byte0[7], not_6_out, not_7_out, not_8_out);
  and and_8 (and_8_out, not_1_out, not_4_out, not_5_out, not_6_out, Byte0[5], not_8_out);
  and and_9 (and_9_out, not_1_out, not_2_out, not_3_out, not_4_out, not_6_out, Byte0[5]);
  and and_10 (and_10_out, not_1_out, not_2_out, not_3_out, not_4_out, not_5_out, Byte0[6], not_7_out);
  and and_11 (and_11_out, not_1_out, not_2_out, not_5_out, Byte0[5], not_8_out);
  and and_12 (and_12_out, not_1_out, not_3_out, not_5_out, not_6_out, Byte0[5], not_8_out);
  and and_13 (and_13_out, not_1_out, not_2_out, not_3_out, not_4_out, not_5_out);
  and and_14 (and_14_out, not_1_out, not_2_out, not_3_out, not_4_out, not_6_out);
  and and_15 (and_15_out, not_1_out, not_3_out, not_5_out, not_6_out, Byte0[5], not_8_out);
  and and_16 (and_16_out, not_1_out, not_3_out, not_5_out, Byte0[6], Byte0[5], Byte0[4]);
  and and_17 (and_17_out, not_1_out, not_4_out, not_5_out, not_6_out, Byte0[5], not_8_out);
  and and_18 (and_18_out, not_1_out, not_4_out, not_5_out, Byte0[6], Byte0[5], Byte0[4]);
  and and_19 (and_19_out, not_1_out, not_2_out, not_5_out, Byte0[5], not_8_out);
  and and_20 (and_20_out, not_1_out, not_2_out, not_5_out, Byte0[6], Byte0[5]);
  or or_1 (NeedValC, and_2_out, and_3_out, and_4_out, and_5_out, and_6_out, and_7_out);
  or or_2 (NeedRegIds, and_8_out, and_9_out, and_10_out, and_11_out, and_12_out);
  or or_3 (InstrValid, and_13_out, and_14_out, and_15_out, and_16_out, and_17_out, and_18_out, and_19_out, and_20_out);

  // Notes on the sheet:
  //   0-3: icode
  //   4-7: ifun
endmodule

module next_PC (
  input  NeedValC,
  input  NeedRegids,
  input  [11:0] PC,
  output [63:0] valP
);

  wire [11:0] adder_1_out, adder_2_out, adder_3_out, bit_extender_1_out, bit_extender_2_out, shifter_1_out;

  assign bit_extender_1_out = {{11{1'b0}}, NeedValC};  // Bit_Extender bit_extender_1
  assign bit_extender_2_out = {{11{1'b0}}, NeedRegids};  // Bit_Extender bit_extender_2
  Shifter #(.width(12)) shifter_1 (.in(bit_extender_1_out), .\dist (4'b0011), .out(shifter_1_out));
  Adder #(.width(12)) adder_1 (.a(12'h1), .b(PC), .out(adder_1_out));  // open: cin, cout
  Adder #(.width(12)) adder_2 (.a(bit_extender_2_out), .b(adder_1_out), .out(adder_2_out));  // open: cin, cout
  Adder #(.width(12)) adder_3 (.a(shifter_1_out), .b(adder_2_out), .out(adder_3_out));  // open: cin, cout
  assign valP = {{52{1'b0}}, adder_3_out};  // Bit_Extender bit_extender_3
endmodule

module Decode_Unit (
  input  [3:0] dstE,
  input  [63:0] valE,
  input  [3:0] srcA,
  input  [3:0] srcB,
  input  [3:0] dstM,
  input  [63:0] valM,
  input  CLK,
  input  WE,
  output [63:0] valA,
  output [63:0] valB
);

  wire and_1_out, and_2_out, and_3_out, and_4_out, and_5_out, and_6_out, and_7_out, and_8_out, and_9_out,
       and_10_out, and_11_out, and_12_out, and_13_out, and_14_out, and_15_out, decoder_1_out0,
       decoder_1_out1, decoder_1_out2, decoder_1_out3, decoder_1_out4, decoder_1_out5, decoder_1_out6,
       decoder_1_out7, decoder_1_out8, decoder_1_out9, decoder_1_out10, decoder_1_out11, decoder_1_out12,
       decoder_1_out13, decoder_1_out14, decoder_2_out0, decoder_2_out1, decoder_2_out2, decoder_2_out3,
       decoder_2_out4, decoder_2_out5, decoder_2_out6, decoder_2_out7, decoder_2_out8, decoder_2_out9,
       decoder_2_out10, decoder_2_out11, decoder_2_out12, decoder_2_out13, decoder_2_out14, or_1_out,
       or_2_out, or_3_out, or_4_out, or_5_out, or_6_out, or_7_out, or_8_out, or_9_out, or_10_out, or_11_out,
       or_12_out, or_13_out, or_14_out, or_15_out;
  wire [63:0] multiplexer_1_out, multiplexer_2_out, multiplexer_3_out, multiplexer_4_out, multiplexer_5_out,
       multiplexer_6_out, multiplexer_7_out, multiplexer_8_out, multiplexer_9_out, multiplexer_10_out,
       multiplexer_11_out, multiplexer_12_out, multiplexer_13_out, multiplexer_14_out, multiplexer_15_out,
       R_r8_q, R_r9_q, R_r10_q, R_r11_q, R_r12_q, R_r13_q, R_r14_q, R_rax_q, R_rbp_q, R_rbx_q, R_rcx_q,
       R_rdi_q, R_rdx_q, R_rsi_q, R_rsp_q;

  Decoder #(.select(4)) decoder_1 (
    .out0(decoder_1_out0), .out1(decoder_1_out1), .out2(decoder_1_out2), .out3(decoder_1_out3),
    .out4(decoder_1_out4), .out5(decoder_1_out5), .out6(decoder_1_out6), .out7(decoder_1_out7),
    .out8(decoder_1_out8), .out9(decoder_1_out9), .out10(decoder_1_out10), .out11(decoder_1_out11),
    .out12(decoder_1_out12), .out13(decoder_1_out13), .out14(decoder_1_out14), .sel(dstE), .en(1'b1));  // open: out15
  Decoder #(.select(4)) decoder_2 (
    .out0(decoder_2_out0), .out1(decoder_2_out1), .out2(decoder_2_out2), .out3(decoder_2_out3),
    .out4(decoder_2_out4), .out5(decoder_2_out5), .out6(decoder_2_out6), .out7(decoder_2_out7),
    .out8(decoder_2_out8), .out9(decoder_2_out9), .out10(decoder_2_out10), .out11(decoder_2_out11),
    .out12(decoder_2_out12), .out13(decoder_2_out13), .out14(decoder_2_out14), .sel(dstM), .en(1'b1));  // open: out15
  or or_1 (or_1_out, decoder_1_out0, decoder_2_out0);
  or or_2 (or_2_out, decoder_1_out1, decoder_2_out1);
  or or_3 (or_3_out, decoder_1_out2, decoder_2_out2);
  or or_4 (or_4_out, decoder_1_out3, decoder_2_out3);
  or or_5 (or_5_out, decoder_1_out4, decoder_2_out4);
  or or_6 (or_6_out, decoder_1_out5, decoder_2_out5);
  or or_7 (or_7_out, decoder_1_out6, decoder_2_out6);
  or or_8 (or_8_out, decoder_1_out7, decoder_2_out7);
  or or_9 (or_9_out, decoder_1_out8, decoder_2_out8);
  or or_10 (or_10_out, decoder_1_out9, decoder_2_out9);
  or or_11 (or_11_out, decoder_1_out10, decoder_2_out10);
  or or_12 (or_12_out, decoder_1_out11, decoder_2_out11);
  or or_13 (or_13_out, decoder_1_out12, decoder_2_out12);
  or or_14 (or_14_out, decoder_1_out13, decoder_2_out13);
  or or_15 (or_15_out, decoder_1_out14, decoder_2_out14);
  Multiplexer #(.width(64)) multiplexer_1 (.in0(valM), .in1(valE), .out(multiplexer_1_out), .sel(decoder_2_out0));
  and and_1 (and_1_out, or_1_out, WE);
  Multiplexer #(.width(64)) multiplexer_2 (.in0(valM), .in1(valE), .out(multiplexer_2_out), .sel(decoder_2_out1));
  and and_2 (and_2_out, or_2_out, WE);
  Multiplexer #(.width(64)) multiplexer_3 (.in0(valE), .in1(valM), .out(multiplexer_3_out), .sel(decoder_2_out2));
  and and_3 (and_3_out, or_3_out, WE);
  Multiplexer #(.width(64)) multiplexer_4 (.in0(valE), .in1(valM), .out(multiplexer_4_out), .sel(decoder_2_out3));
  and and_4 (and_4_out, or_4_out, WE);
  Multiplexer #(.width(64)) multiplexer_5 (.in0(valE), .in1(valM), .out(multiplexer_5_out), .sel(decoder_2_out4));
  and and_5 (and_5_out, or_5_out, WE);
  Multiplexer #(.width(64)) multiplexer_6 (.in0(valE), .in1(valM), .out(multiplexer_6_out), .sel(decoder_2_out5));
  and and_6 (and_6_out, or_6_out, WE);
  Multiplexer #(.width(64)) multiplexer_7 (.in0(valE), .in1(valM), .out(multiplexer_7_out), .sel(decoder_2_out6));
  and and_7 (and_7_out, or_7_out, WE);
  Multiplexer #(.width(64)) multiplexer_8 (.in0(valE), .in1(valM), .out(multiplexer_8_out), .sel(decoder_2_out7));
  and and_8 (and_8_out, or_8_out, WE);
  Multiplexer #(.width(64)) multiplexer_9 (.in0(valE), .in1(valM), .out(multiplexer_9_out), .sel(decoder_2_out8));
  and and_9 (and_9_out, or_9_out, WE);
  Multiplexer #(.width(64)) multiplexer_10 (.in0(valE), .in1(valM), .out(multiplexer_10_out), .sel(decoder_2_out9));
  and and_10 (and_10_out, or_10_out, WE);
  Multiplexer #(.width(64)) multiplexer_11 (.in0(valE), .in1(valM), .out(multiplexer_11_out), .sel(decoder_2_out10));
  and and_11 (and_11_out, or_11_out, WE);
  Multiplexer #(.width(64)) multiplexer_12 (.in0(valE), .in1(valM), .out(multiplexer_12_out), .sel(decoder_2_out11));
  and and_12 (and_12_out, or_12_out, WE);
  Multiplexer #(.width(64)) multiplexer_13 (.in0(valE), .in1(valM), .out(multiplexer_13_out), .sel(decoder_2_out12));
  and and_13 (and_13_out, or_13_out, WE);
  Multiplexer #(.width(64)) multiplexer_14 (.in0(valE), .in1(valM), .out(multiplexer_14_out), .sel(decoder_2_out13));
  and and_14 (and_14_out, or_14_out, WE);
  Multiplexer #(.width(64)) multiplexer_15 (.in0(valE), .in1(valM), .out(multiplexer_15_out), .sel(decoder_2_out14));
  and and_15 (and_15_out, or_15_out, WE);
  Register #(.width(64)) R_rax (.D(multiplexer_1_out), .en(and_1_out), .clk(CLK), .Q(R_rax_q));  // open: clr
  Register #(.width(64)) R_rcx (.D(multiplexer_2_out), .en(and_2_out), .clk(CLK), .Q(R_rcx_q));  // open: clr
  Register #(.width(64)) R_rdx (.D(multiplexer_3_out), .en(and_3_out), .clk(CLK), .Q(R_rdx_q));  // open: clr
  Register #(.width(64)) R_rbx (.D(multiplexer_4_out), .en(and_4_out), .clk(CLK), .Q(R_rbx_q));  // open: clr
  Register #(.width(64)) R_rsp (.D(multiplexer_5_out), .en(and_5_out), .clk(CLK), .Q(R_rsp_q));  // open: clr
  Register #(.width(64)) R_rbp (.D(multiplexer_6_out), .en(and_6_out), .clk(CLK), .Q(R_rbp_q));  // open: clr
  Register #(.width(64)) R_rsi (.D(multiplexer_7_out), .en(and_7_out), .clk(CLK), .Q(R_rsi_q));  // open: clr
  Register #(.width(64)) R_rdi (.D(multiplexer_8_out), .en(and_8_out), .clk(CLK), .Q(R_rdi_q));  // open: clr
  Register #(.width(64)) R_r8 (.D(multiplexer_9_out), .en(and_9_out), .clk(CLK), .Q(R_r8_q));  // open: clr
  Register #(.width(64)) R_r9 (.D(multiplexer_10_out), .en(and_10_out), .clk(CLK), .Q(R_r9_q));  // open: clr
  Register #(.width(64)) R_r10 (.D(multiplexer_11_out), .en(and_11_out), .clk(CLK), .Q(R_r10_q));  // open: clr
  Register #(.width(64)) R_r11 (.D(multiplexer_12_out), .en(and_12_out), .clk(CLK), .Q(R_r11_q));  // open: clr
  Register #(.width(64)) R_r12 (.D(multiplexer_13_out), .en(and_13_out), .clk(CLK), .Q(R_r12_q));  // open: clr
  Register #(.width(64)) R_r13 (.D(multiplexer_14_out), .en(and_14_out), .clk(CLK), .Q(R_r13_q));  // open: clr
  Register #(.width(64)) R_r14 (.D(multiplexer_15_out), .en(and_15_out), .clk(CLK), .Q(R_r14_q));  // open: clr
  Multiplexer #(.select(4), .width(64)) multiplexer_16 (
    .in0(R_rax_q), .in1(R_rcx_q), .in2(R_rdx_q), .in3(R_rbx_q), .in4(R_rsp_q), .in5(R_rbp_q), .in6(R_rsi_q),
    .in7(R_rdi_q), .in8(R_r8_q), .in9(R_r9_q), .in10(R_r10_q), .in11(R_r11_q), .in12(R_r12_q),
    .in13(R_r13_q), .in14(R_r14_q), .out(valA), .sel(srcA));  // open: in15
  Multiplexer #(.select(4), .width(64)) multiplexer_17 (
    .in0(R_rax_q), .in1(R_rcx_q), .in2(R_rdx_q), .in3(R_rbx_q), .in4(R_rsp_q), .in5(R_rbp_q), .in6(R_rsi_q),
    .in7(R_rdi_q), .in8(R_r8_q), .in9(R_r9_q), .in10(R_r10_q), .in11(R_r11_q), .in12(R_r12_q),
    .in13(R_r13_q), .in14(R_r14_q), .out(valB), .sel(srcB));  // open: in15

  // Notes on the sheet:
  //   Execute Write Port
  //   Memory Write Port
  //   Register A Read port
  //   Register B Read port
endmodule

module srcA (
  input  [3:0] icode,
  input  [3:0] rA,
  output [3:0] src_A
);

  wire decoder_1_out2, decoder_1_out4, decoder_1_out6, decoder_1_out10, or_1_out;

  Decoder #(.select(4)) decoder_1 (
    .out2(decoder_1_out2), .out4(decoder_1_out4), .out6(decoder_1_out6), .out10(decoder_1_out10), .sel(icode));  // open: out0, out1, out3, out5, out7, out8, out9, out11, out12, out13, out14, out15, en
  or or_1 (or_1_out, decoder_1_out2, decoder_1_out4, decoder_1_out6, decoder_1_out10);
  Multiplexer #(.width(4)) multiplexer_1 (.in0(4'b1111), .in1(rA), .out(src_A), .sel(or_1_out));
endmodule

module srcB (
  input  [3:0] icode,
  input  [3:0] rB,
  output [3:0] src_B
);

  wire decoder_1_out2, decoder_1_out4, decoder_1_out6, decoder_1_out10, or_1_out;

  Decoder #(.select(4)) decoder_1 (
    .out2(decoder_1_out2), .out4(decoder_1_out4), .out6(decoder_1_out6), .out10(decoder_1_out10), .sel(icode));  // open: out0, out1, out3, out5, out7, out8, out9, out11, out12, out13, out14, out15, en
  or or_1 (or_1_out, decoder_1_out2, decoder_1_out4, decoder_1_out6, decoder_1_out10);
  Multiplexer #(.width(4)) multiplexer_1 (.in0(4'b1111), .in1(rB), .out(src_B), .sel(or_1_out));
endmodule

module dstM (
  input  [3:0] icode,
  input  [3:0] rA,
  output [3:0] dst_M
);

  wire decoder_1_out5, decoder_1_out11, or_1_out;

  Decoder #(.select(4)) decoder_1 (
    .out5(decoder_1_out5), .out11(decoder_1_out11), .sel(icode));  // open: out0, out1, out2, out3, out4, out6, out7, out8, out9, out10, out12, out13, out14, out15, en
  or or_1 (or_1_out, decoder_1_out5, decoder_1_out11);
  Multiplexer #(.width(4)) multiplexer_1 (.in0(4'b1111), .in1(rA), .out(dst_M), .sel(or_1_out));
endmodule

module Execute_unit (
  input  [3:0] icode,
  input  [63:0] ValA,
  input  [63:0] ValC,
  input  [63:0] ValB,
  input  [3:0] ifun,
  input  clk,
  output setCC,
  output cf,
  output zf,
  output [63:0] valE,
  output SF,
  output OF_Flag
);

  wire adder_1_cout, and_2_out, and_3_out, and_5_out, and_6_out, and_7_out, and_8_out, and_9_out,
       comparator_1_eq, comparator_2_lt, comparator_3_eq, not_1_out, not_2_out, not_3_out, not_4_out,
       not_5_out, or_1_out, or_2_out, or_3_out, subtractor_1_bout;
  wire [1:0] multiplexer_1_out, multiplexer_4_out;
  wire [62:0] multiplexer_2_out, multiplexer_3_out, multiplexer_5_out;
  wire [63:0] adder_1_out, and_4_out, subtractor_1_out, xor_1_out;
  wire [63:63] multiplexer_2_out_2, multiplexer_3_out_2, multiplexer_5_out_2;

  Multiplexer #(.select(4), .width(2)) multiplexer_1 (
    .in0(2'b00), .in1(2'b01), .in2(2'b10), .in3(2'b11), .in4(2'b00), .in5(2'b00), .in6(2'b00),
    .out(multiplexer_1_out), .sel(ifun));  // open: in7, in8, in9, in10, in11, in12, in13, in14, in15
  Multiplexer #(.select(4), .width(64)) multiplexer_2 (
    .in0(ValA), .in1(ValA), .in2(ValA), .in3(ValC), .in4(ValC), .in5(ValC), .in6(ValA),
    .in8(64'hfffffffffffffff8), .in9(64'hfffffffffffffff8), .in10(64'hfffffffffffffff8),
    .in11(64'hfffffffffffffff8), .out({multiplexer_2_out_2[63], multiplexer_2_out}), .sel(icode));  // open: in7, in12, in13, in14, in15
  Multiplexer #(.select(4), .width(64)) multiplexer_3 (
    .in0({64{1'b0}}), .in1({64{1'b0}}), .in2({64{1'b0}}), .in3({64{1'b0}}), .in4(ValB), .in5(ValB),
    .in6(ValB), .in8(ValB), .in9(ValB), .in10(ValB), .in11(ValB),
    .out({multiplexer_3_out_2[63], multiplexer_3_out}), .sel(icode));  // open: in7, in12, in13, in14, in15
  Multiplexer #(.select(4), .width(2)) multiplexer_4 (
    .in0(2'b00), .in1(2'b00), .in2(2'b00), .in3(2'b00), .in4(2'b00), .in5(2'b00), .in6(multiplexer_1_out),
    .in7(2'b00), .in8(2'b00), .in9(2'b00), .in10(2'b00), .in11(2'b00), .out(multiplexer_4_out), .sel(icode));  // open: in12, in13, in14, in15
  not not_1 (not_1_out, icode[0]);
  not not_2 (not_2_out, icode[3]);
  and and_1 (setCC, not_1_out, icode[1], icode[2], not_2_out);
  Comparator #(.mode("unsigned"), .width(4)) comparator_1 (
    .a(ifun), .b(4'b0000), .eq(comparator_1_eq));  // open: gt, lt
  and and_2 (and_2_out, multiplexer_2_out_2[63], multiplexer_3_out_2[63]);
  Adder #(.width(64)) adder_1 (
    .a({multiplexer_2_out_2[63], multiplexer_2_out}), .b({multiplexer_3_out_2[63], multiplexer_3_out}),
    .out(adder_1_out), .cout(adder_1_cout));  // open: cin
  and and_3 (and_3_out, adder_1_cout, comparator_1_eq);
  Subtractor #(.width(64)) subtractor_1 (
    .a({multiplexer_3_out_2[63], multiplexer_3_out}), .b({multiplexer_2_out_2[63], multiplexer_2_out}),
    .out(subtractor_1_out), .bout(subtractor_1_bout));  // open: bin
  assign and_4_out = {multiplexer_2_out_2[63], multiplexer_2_out} & {multiplexer_3_out_2[63], multiplexer_3_out};  // AND_Gate and_4, 64 bits wide
  assign xor_1_out = {multiplexer_2_out_2[63], multiplexer_2_out} ^ {multiplexer_3_out_2[63], multiplexer_3_out};  // XOR_Gate xor_1, 64 bits wide
  not not_3 (not_3_out, multiplexer_2_out_2[63]);
  not not_4 (not_4_out, multiplexer_3_out_2[63]);
  and and_5 (and_5_out, multiplexer_2_out_2[63], multiplexer_3_out_2[63]);
  and and_6 (and_6_out, not_3_out, not_4_out);
  not not_5 (not_5_out, multiplexer_5_out_2[63]);
  or or_1 (or_1_out, and_5_out, and_6_out);
  and and_7 (and_7_out, not_3_out, multiplexer_5_out_2[63]);
  and and_8 (and_8_out, multiplexer_2_out_2[63], not_5_out);
  Comparator #(.width(64)) comparator_2 (
    .a({multiplexer_5_out_2[63], multiplexer_5_out}), .b({multiplexer_2_out_2[63], multiplexer_2_out}),
    .lt(comparator_2_lt));  // open: gt, eq
  Comparator #(.width(64)) comparator_3 (
    .a({64{1'b0}}), .b({multiplexer_5_out_2[63], multiplexer_5_out}), .eq(comparator_3_eq));  // open: gt, lt
  Multiplexer #(.select(2), .width(64)) multiplexer_5 (
    .in0(adder_1_out), .in1(subtractor_1_out), .in2(and_4_out), .in3(xor_1_out),
    .out({multiplexer_5_out_2[63], multiplexer_5_out}), .sel(multiplexer_4_out));
  or or_2 (or_2_out, and_7_out, and_8_out);
  Register #(.width(1)) register_1 (.D(comparator_2_lt), .en(setCC), .clk(clk), .Q(cf));  // open: clr
  Register #(.width(1)) register_2 (.D(and_9_out), .en(setCC), .clk(clk));  // open: Q, clr
  and and_9 (and_9_out, or_1_out, or_2_out);
  Register #(.width(64)) register_3 (
    .D({multiplexer_5_out_2[63], multiplexer_5_out}), .clk(clk), .Q(valE));  // open: en, clr
  Register #(.width(1)) register_4 (.D(or_3_out), .en(setCC), .clk(clk), .Q(SF));  // open: clr
  or or_3 (or_3_out, and_2_out, adder_1_out[63], subtractor_1_bout);
  Register #(.width(1)) register_5 (.D(comparator_3_eq), .en(setCC), .clk(clk), .Q(zf));  // open: clr
  Register #(.width(1)) register_6 (.D(and_3_out), .en(setCC), .clk(clk), .Q(OF_Flag));  // open: clr

  // Notes on the sheet:
  //   OPq
  //   ALU_A
  //   ALU_B
  //   ALU_func
  //   +
  //   -
  //   AND
  //   XOR
endmodule

module memory (
  input  [63:0] valP,
  input  CLK,
  input  [63:0] valA,
  input  [3:0] icode,
  input  [63:0] valE,
  output [63:0] ValM
);

  wire multiplexer_3_out, multiplexer_4_out;
  wire [11:0] multiplexer_2_out;
  wire [63:0] multiplexer_1_out;

  Multiplexer #(.select(4), .width(64)) multiplexer_1 (
    .in4(valA), .in8(valP), .in10(valA), .out(multiplexer_1_out), .sel(icode));  // open: in0, in1, in2, in3, in5, in6, in7, in9, in11, in12, in13, in14, in15
  Multiplexer #(.select(4), .width(12)) multiplexer_2 (
    .in4(valE[11:0]), .in5(valE[11:0]), .in8(valE[11:0]), .in9(valA[11:0]), .in10(valE[11:0]),
    .in11(valA[11:0]), .out(multiplexer_2_out), .sel(icode));  // open: in0, in1, in2, in3, in6, in7, in12, in13, in14, in15
  Multiplexer #(.select(4)) multiplexer_3 (
    .in0(1'b0), .in1(1'b0), .in2(1'b0), .in3(1'b0), .in4(1'b1), .in5(1'b0), .in6(1'b0), .in7(1'b0),
    .in8(1'b1), .in9(1'b0), .in10(1'b1), .in11(1'b0), .out(multiplexer_3_out), .sel(icode));  // open: in12, in13, in14, in15
  Multiplexer #(.select(4)) multiplexer_4 (
    .in0(1'b0), .in1(1'b0), .in2(1'b0), .in3(1'b0), .in4(1'b1), .in5(1'b0), .in6(1'b0), .in7(1'b0),
    .in8(1'b1), .in9(1'b0), .in10(1'b1), .in11(1'b0), .out(multiplexer_4_out), .sel(icode));  // open: in12, in13, in14, in15
  RAM #(.addrWidth(12), .dataWidth(64)) ram_1 (
    .addr(multiplexer_2_out), .we(multiplexer_4_out), .oe(multiplexer_3_out), .clk(CLK),
    .din(multiplexer_1_out), .dout(ValM));

  // Notes on the sheet:
  //   MemData
  //   MemAddr
  //   Mem_read
  //   Memwrite
endmodule

module dstE (
  input  [3:0] icode,
  input  [3:0] rB,
  output [3:0] dst_E
);

  wire decoder_1_out2, decoder_1_out3, decoder_1_out6, decoder_1_out8, decoder_1_out9, decoder_1_out10,
       decoder_1_out11, or_1_out;

  Decoder #(.select(4)) decoder_1 (
    .out2(decoder_1_out2), .out3(decoder_1_out3), .out6(decoder_1_out6), .out8(decoder_1_out8),
    .out9(decoder_1_out9), .out10(decoder_1_out10), .out11(decoder_1_out11), .sel(icode));  // open: out0, out1, out4, out5, out7, out12, out13, out14, out15, en
  or or_1 (or_1_out, decoder_1_out2, decoder_1_out3, decoder_1_out6, decoder_1_out8, decoder_1_out9, decoder_1_out10, decoder_1_out11);
  Multiplexer #(.width(4)) multiplexer_1 (.in0(4'b1111), .in1(rB), .out(dst_E), .sel(or_1_out));
endmodule

module ME_Enable (
  input  [3:0] icode
);

  wire not_1_out, not_3_out;

  not not_1 (not_1_out, icode[3]);
  // NOT_Gate not_2 has open pins: in=icode[2], out=open
  not not_3 (not_3_out, icode[1]);
  // NOT_Gate not_4 has open pins: in=icode[0], out=open
  // AND_Gate and_1 has open pins: in0=not_1_out, in1=icode[2], in2=not_3_out, in3=icode[0], out=open
endmodule

module Scratch_Decode (
  input  [3:0] rA,
  input  [3:0] icode,
  input  [3:0] rB,
  output [3:0] ValA,
  output [3:0] ValB
);

  wire clock_1_out;
  wire [3:0] multiplexer_1_out, multiplexer_2_out, undriven;

  Multiplexer #(.select(4), .width(4)) multiplexer_1 (
    .in0(4'b1111), .in1(4'b1111), .in2(rA), .in3(4'b1111), .in4(rA), .in5(4'b1111), .in6(rA), .in7(4'b1111),
    .in8(undriven), .in9(undriven), .in10(rA), .in11(undriven), .out(multiplexer_1_out), .sel(icode));  // open: in12, in13, in14, in15
  Multiplexer #(.select(4), .width(4)) multiplexer_2 (
    .in0(4'b1111), .in1(4'b1111), .in2(4'b1111), .in3(4'b1111), .in4(rB), .in5(rB), .in6(rB), .in7(4'b1111),
    .in8(4'b1111), .in9(undriven), .in10(undriven), .in11(undriven), .out(multiplexer_2_out), .sel(icode));  // open: in12, in13, in14, in15
  Register #(.width(4)) register_1 (.D(multiplexer_1_out), .clk(clock_1_out), .Q(ValA));  // open: en, clr
  Register #(.width(4)) register_2 (.D(multiplexer_2_out), .clk(clock_1_out), .Q(ValB));  // open: en, clr
  Clock clock_1 (.out(clock_1_out));

  // Notes on the sheet:
  //   srcB
endmodule

module PC_update (
  input  [63:0] valC,
  input  Cnd,
  input  [63:0] valM,
  input  [63:0] valP,
  input  [3:0] icode,
  output [11:0] newPC
);

  wire [11:0] multiplexer_1_out;

  Multiplexer #(.width(12)) multiplexer_1 (.in0(valP[11:0]), .in1(valC[11:0]), .out(multiplexer_1_out), .sel(Cnd));
  Multiplexer #(.select(4), .width(12)) multiplexer_2 (
    .in0(valP[11:0]), .in1(valP[11:0]), .in2(valP[11:0]), .in3(valP[11:0]), .in4(valP[11:0]),
    .in5(valP[11:0]), .in6(valP[11:0]), .in7(multiplexer_1_out), .in8(valC[11:0]), .in9(valM[11:0]),
    .in10(valP[11:0]), .in11(valP[11:0]), .out(newPC), .sel(icode));  // open: in12, in13, in14, in15
endmodule

module jmpCond (
  input  ZF,
  input  SF,
  input  OF_flag,
  input  [3:0] ifun,
  output JumpCnd
);

  wire and_1_out, not_1_out, not_2_out, or_1_out, xor_1_out;

  xor xor_1 (xor_1_out, SF, OF_flag);
  or or_1 (or_1_out, ZF, xor_1_out);
  not not_1 (not_1_out, xor_1_out);
  not not_2 (not_2_out, ZF);
  and and_1 (and_1_out, not_2_out, not_1_out);
  Multiplexer #(.select(4)) multiplexer_1 (
    .in0(1'b1), .in1(or_1_out), .in2(xor_1_out), .in3(ZF), .in4(not_2_out), .in5(not_1_out), .in6(and_1_out),
    .in7(1'b0), .in8(1'b0), .in9(1'b0), .in10(1'b0), .in11(1'b0), .in12(1'b0), .in13(1'b0), .in14(1'b0),
    .in15(1'b0), .out(JumpCnd), .sel(ifun));
endmodule

module totalCC (
  input  ZF,
  input  SF,
  input  OFflag,
  input  [3:0] ifun,
  input  [3:0] icode,
  input  SetCC,
  output FinalCC
);

  wire cmov_circuit_1_cc, jmpcond_1_jumpcnd, multiplexer_1_out;

  jmpCond jmpcond_1 (.ZF(ZF), .SF(SF), .OF_flag(OFflag), .ifun(ifun), .JumpCnd(jmpcond_1_jumpcnd));
  cmov_circuit cmov_circuit_1 (.ZF(ZF), .SF(SF), .OverF(OFflag), .ifun(ifun), .CC(cmov_circuit_1_cc));
  Multiplexer #(.select(4)) multiplexer_1 (
    .in2(cmov_circuit_1_cc), .in7(jmpcond_1_jumpcnd), .out(multiplexer_1_out), .sel(icode));  // open: in0, in1, in3, in4, in5, in6, in8, in9, in10, in11, in12, in13, in14, in15
  Multiplexer multiplexer_2 (.in0(multiplexer_1_out), .in1(1'b0), .out(FinalCC), .sel(SetCC));
endmodule

module cmov_circuit (
  input  ZF,
  input  SF,
  input  OverF,
  input  [3:0] ifun,
  output CC
);

  wire and_1_out, not_1_out, not_2_out, or_1_out, xor_1_out;

  xor xor_1 (xor_1_out, SF, OverF);
  or or_1 (or_1_out, xor_1_out, ZF);
  not not_1 (not_1_out, ZF);
  and and_1 (and_1_out, not_1_out, not_2_out);
  not not_2 (not_2_out, xor_1_out);
  Multiplexer #(.select(4)) multiplexer_1 (
    .in0(1'b0), .in1(or_1_out), .in2(xor_1_out), .in3(ZF), .in4(not_1_out), .in5(not_2_out), .in6(and_1_out),
    .in7(1'b0), .in8(1'b0), .in9(1'b0), .in10(1'b0), .in11(1'b0), .in12(1'b0), .in13(1'b0), .in14(1'b0),
    .in15(1'b0), .out(CC), .sel(ifun));
endmodule

module clockTracker (
  input  clk,
  output [3:0] cycleCount
);

  wire comparator_1_eq;

  Counter #(.max('hf), .width(4)) counter_1 (
    .clr(comparator_1_eq), .clk(clk), .Q(cycleCount));  // open: load, up, count, D, carry
  Comparator #(.mode("unsigned"), .width(4)) comparator_1 (
    .a(4'b1111), .b(cycleCount), .eq(comparator_1_eq));  // open: gt, lt
endmodule

module SetFlags1 (
  input  [7:0] Byte0,
  output NeedValC,
  output NeedRegIds
);

  Multiplexer #(.select(4)) multiplexer_1 (
    .in0(1'b0), .in1(1'b0), .in2(1'b0), .in3(1'b1), .in4(1'b1), .in5(1'b1), .in6(1'b0), .in7(1'b1),
    .in8(1'b1), .in9(1'b0), .in10(1'b0), .in11(1'b0), .out(NeedValC), .sel(Byte0[7:4]));  // open: in12, in13, in14, in15
  Multiplexer #(.select(4)) multiplexer_2 (
    .in0(1'b0), .in1(1'b0), .in2(1'b1), .in3(1'b1), .in4(1'b1), .in5(1'b1), .in6(1'b1), .in7(1'b0),
    .in8(1'b0), .in9(1'b0), .in10(1'b1), .in11(1'b1), .out(NeedRegIds), .sel(Byte0[7:4]));  // open: in12, in13, in14, in15

  // Notes on the sheet:
  //   0-3: icode
  //   4-7: ifun
endmodule
